# Fritzing sketch circuit_diagram (saved by Fritzing 0.9.3b)
circuit board: 8.46667cm x 5.64444cm
breadboards: 1

parts:
  Arduino_Nano = Arduino Nano (Rev3.0)
  Buzzer = Piezo Speaker
  Temp_Sensor = TMP36 [package=to-92]
  RTC = Adafruit DS3231 [part_number="Adafruit #3013"]
  Warning_LED = LED - 5mm [color="Red (633nm)" package="5 mm [THT]"]
  LED_Resistor = Resistor [tolerance=±5% resistance=220 package=THT]

nets:
  N1: Arduino_Nano.RESET, RTC.!RTC_RST
  GND: Arduino_Nano.GND, Buzzer.pin1, Temp_Sensor.GND, RTC.GND, Warning_LED.cathode
  N2: Arduino_Nano.D2, Buzzer.pin2
  N3: Arduino_Nano.D5, LED_Resistor.Pin_1
  5V: Arduino_Nano.5V, RTC.Vin
  N4: Arduino_Nano.A5, RTC.SCL
  N5: Arduino_Nano.A4, RTC.SDA
  N6: Arduino_Nano.A1, Temp_Sensor.VOUT
  3V3: Arduino_Nano.AREF, Arduino_Nano.3V3, Temp_Sensor.VCC
  N7: Warning_LED.anode, LED_Resistor.Pin_0

custom parts:
  Adafruit DS3231: The datasheet for the DS3231 explains that this part is an "Extremely Accurate I²C-Integrated RTC/TCXO/Crystal". And, hey, it does exactly what it says on the tin! This Real Time Clock (RTC) is the most precise you can get in a small, low power package. Most RTCs use an external 32kHz timing crystal that is used to keep time with low current draw. And that's all well and good, but those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
